# Fritzing sketch Security System (saved by Fritzing 0.9.2b)
breadboards: 1

parts:
  Part1 = Arduino Uno (Rev3)
  LED1 = RGB LED (com. cathode, rgb) [package="5 mm [THT]"]
  R1 = Resistor [tolerance=±5% resistance=220 package=THT]
  R2 = Resistor [tolerance=±5% resistance=220 package=THT]
  R3 = Resistor [tolerance=±5% resistance=220 package=THT]
  S1 = Pushbutton [package="[THT]"]
  S2 = Reed switch [package=THT]
  J1 = Basic Servo
  RFID = Header 4 [package=molex-1x4_lock]

nets:
  N1: Part1.D8, RFID.SOUT
  N2: Part1.D9_PWM, R1.Pin_1
  N3: Part1.D10_PWM/SS, R2.Pin_1
  N4: Part1.D11_PWM/MOSI, R3.Pin_1
  N5: Part1.D12/MISO, S1.Pin_1, S1.Pin_2
  N6: Part1.D5_PWM, S2.pin_1
  N7: Part1.D6_PWM, J1.pulse
  N8: Part1.D7, RFID./ENABLE
  VCC: Part1.5V, S1.Pin_3, S1.Pin_4, J1.vcc, RFID.VCC
  GND: Part1.GND, LED1.common_cathode, S2.pin_2, J1.gnd, RFID.GND
  N9: LED1.red_anode, R1.Pin_0
  N10: LED1.green_anode, R2.Pin_0
  N11: LED1.blue_anode, R3.Pin_0

custom parts:
  Header 4: Header 4 Standard 4-pin 0.1 header. Use with straight break away headers (SKU : PRT-00116), right angle break away headers (PRT-00553), swiss pins (PRT-00743), machine pins (PRT-00117), and female headers (PRT-00115). Molex polarized connector foot print use with SKU : PRT-08231 with associated crimp pins and housings. 1MM SMD Version SKU: PRT-10208
